// Logisim project dcdraft.circ as structural Verilog: 3 circuits, main circuit main
module main (
  input  in_1,
  output out_2
);

  wire and_1_out, and_2_out, button_1_out, d_ff_1_q, d_ff_1_qn, d_ff_2_q, d_ff_2_qn, or_1_out;

  Button button_1 (.out(button_1_out));
  or or_1 (or_1_out, d_ff_1_q, d_ff_2_q);
  and and_1 (and_1_out, d_ff_1_qn, d_ff_2_qn, in_1);
  and and_2 (and_2_out, or_1_out, in_1);
  D_Flip_Flop d_ff_1 (.D(and_1_out), .clk(button_1_out), .Q(d_ff_1_q), .Qn(d_ff_1_qn));  // open: preset, reset
  D_Flip_Flop d_ff_2 (.D(and_2_out), .clk(button_1_out), .Q(d_ff_2_q), .Qn(d_ff_2_qn));  // open: preset, reset
  and and_3 (out_2, d_ff_1_q, in_1);
endmodule

module dec664 (
  input  in_1,
  input  in_2,
  input  in_3,
  input  in_4,
  input  in_5,
  input  in_6
);

  wire decoder_1_out0, decoder_1_out1, decoder_1_out2, decoder_1_out3, decoder_1_out4, decoder_1_out5,
       decoder_1_out6, decoder_1_out7, decoder_2_out0, decoder_2_out1, decoder_2_out2, decoder_2_out3,
       decoder_2_out4, decoder_2_out5, decoder_2_out6, decoder_2_out7;

  Decoder #(.select(3)) decoder_1 (
    .out0(decoder_1_out0), .out1(decoder_1_out1), .out2(decoder_1_out2), .out3(decoder_1_out3),
    .out4(decoder_1_out4), .out5(decoder_1_out5), .out6(decoder_1_out6), .out7(decoder_1_out7),
    .sel({in_6, in_5, in_4}));  // open: en
  Decoder #(.select(3)) decoder_2 (
    .out0(decoder_2_out0), .out1(decoder_2_out1), .out2(decoder_2_out2), .out3(decoder_2_out3),
    .out4(decoder_2_out4), .out5(decoder_2_out5), .out6(decoder_2_out6), .out7(decoder_2_out7),
    .sel({in_3, in_2, in_1}));  // open: en
  // AND_Gate and_1 has open pins: in0=decoder_2_out0, in1=decoder_1_out0, out=open
  // AND_Gate and_2 has open pins: in0=decoder_2_out1, in1=decoder_1_out0, out=open
  // AND_Gate and_3 has open pins: in0=decoder_2_out2, in1=decoder_1_out0, out=open
  // AND_Gate and_4 has open pins: in0=decoder_2_out3, in1=decoder_1_out0, out=open
  // AND_Gate and_5 has open pins: in0=decoder_2_out4, in1=decoder_1_out0, out=open
  // AND_Gate and_6 has open pins: in0=decoder_2_out5, in1=decoder_1_out0, out=open
  // AND_Gate and_7 has open pins: in0=decoder_2_out6, in1=decoder_1_out0, out=open
  // AND_Gate and_8 has open pins: in0=decoder_2_out7, in1=decoder_1_out0, out=open
  // AND_Gate and_9 has open pins: in0=decoder_2_out0, in1=decoder_1_out1, out=open
  // AND_Gate and_10 has open pins: in0=decoder_2_out1, in1=decoder_1_out1, out=open
  // AND_Gate and_11 has open pins: in0=decoder_2_out2, in1=decoder_1_out1, out=open
  // AND_Gate and_12 has open pins: in0=decoder_2_out3, in1=decoder_1_out1, out=open
  // AND_Gate and_13 has open pins: in0=decoder_2_out4, in1=decoder_1_out1, out=open
  // AND_Gate and_14 has open pins: in0=decoder_2_out5, in1=decoder_1_out1, out=open
  // AND_Gate and_15 has open pins: in0=decoder_2_out6, in1=decoder_1_out1, out=open
  // AND_Gate and_16 has open pins: in0=decoder_2_out7, in1=decoder_1_out1, out=open
  // AND_Gate and_17 has open pins: in0=decoder_2_out0, in1=decoder_1_out2, out=open
  // AND_Gate and_18 has open pins: in0=decoder_2_out1, in1=decoder_1_out2, out=open
  // AND_Gate and_19 has open pins: in0=decoder_2_out2, in1=decoder_1_out2, out=open
  // AND_Gate and_20 has open pins: in0=decoder_2_out3, in1=decoder_1_out2, out=open
  // AND_Gate and_21 has open pins: in0=decoder_2_out4, in1=decoder_1_out2, out=open
  // AND_Gate and_22 has open pins: in0=decoder_2_out5, in1=decoder_1_out2, out=open
  // AND_Gate and_23 has open pins: in0=decoder_2_out6, in1=decoder_1_out2, out=open
  // AND_Gate and_24 has open pins: in0=decoder_2_out7, in1=decoder_1_out2, out=open

  // Notes on the sheet:
  //   First 3 bits control all AND gates
  //   3-8 decoder
  //   Last 3 bits control which 8-AND segment
  //   3-8 decoder
  //   D0
  //   D1
  //   D7
  //   D8
  //   D15
  //   Altogether 8x8-AND gates = 64 outputs
  //   D16
  //   D24-31
  //   D23
  //   D40-47
  //   D32-39
  //   D56-63
  //   D48-55
endmodule

module hold3 (
  input  w1,
  input  clk,
  input  w2,
  output z1,
  output z2
);

  wire and_1_out, and_2_out, and_3_out, and_4_out, button_1_out, button_2_out, d_ff_1_q, d_ff_2_q, d_ff_2_qn,
       d_ff_3_q, d_ff_3_qn, d_ff_4_q, d_ff_4_qn, or_1_out, or_2_out, or_3_out, or_4_out, or_5_out, or_6_out,
       or_7_out;

  Button button_1 (.out(button_1_out));
  Button button_2 (.out(button_2_out));
  or or_1 (or_1_out, d_ff_1_q, d_ff_2_q);
  or or_2 (or_2_out, d_ff_1_q, d_ff_2_qn);
  and and_1 (and_1_out, or_1_out, w1);
  and and_2 (and_2_out, or_2_out, w1);
  or or_3 (or_3_out, clk, button_1_out);
  or or_4 (or_4_out, d_ff_3_q, d_ff_4_q);
  or or_5 (or_5_out, clk, button_2_out);
  D_Flip_Flop d_ff_1 (.D(and_1_out), .clk(or_3_out), .Q(d_ff_1_q));  // open: Qn, preset, reset
  D_Flip_Flop d_ff_2 (.D(and_2_out), .clk(or_3_out), .Q(d_ff_2_q), .Qn(d_ff_2_qn));  // open: preset, reset
  D_Flip_Flop d_ff_3 (.D(and_3_out), .clk(or_5_out), .Q(d_ff_3_q), .Qn(d_ff_3_qn));  // open: preset, reset
  and and_3 (and_3_out, or_4_out, w2);
  D_Flip_Flop d_ff_4 (.D(and_4_out), .clk(or_5_out), .Q(d_ff_4_q), .Qn(d_ff_4_qn));  // open: preset, reset
  and and_4 (and_4_out, d_ff_3_qn, d_ff_4_qn, w2);
  LED led_1 (.in(or_6_out));
  or or_6 (or_6_out, d_ff_1_q, d_ff_3_q);
  and and_5 (z1, d_ff_1_q, d_ff_2_q);
  LED led_2 (.in(or_7_out));
  or or_7 (or_7_out, d_ff_2_q, d_ff_4_q);
  and and_6 (z2, d_ff_3_q, w2);

  // Notes on the sheet:
  //   Moore - Hold3 Detector
  //   Dy2 = (y2 + y1)w
  //   Dy1 = (y2 + ~y1)w
  //   z = y1y2
  //   Mealy - Hold3 Detector
  //   Dy2 = w~y2~y1
  //   Dy1 = w(y2+y1)
  //   z = wy2
endmodule
